// Logisim project 10-bitCPU.circ as structural Verilog: 2 circuits, main circuit main
module main (
  input  in_1,
  output [9:0] Output
);

  wire and_1_out, clock_1_out, control_unit_1_ain, control_unit_1_bin, control_unit_1_branch,
       control_unit_1_immidiate, control_unit_1_load, control_unit_1_move, control_unit_1_notequal,
       control_unit_1_readmemory, control_unit_1_unconditional, control_unit_1_writeacc, multiplexer_6_out,
       multiplexer_7_out, n10_bit_alu_1_less, n10_bit_alu_1_zero, not_1_out;
  wire [1:0] control_unit_1_aluop;
  wire [9:0] adder_1_out, adder_2_out, bit_extender_1_out, bit_extender_2_out, multiplexer_1_out,
       multiplexer_2_out, multiplexer_3_out, multiplexer_4_out, multiplexer_5_out, multiplexer_8_out,
       n10_bit_alu_1_result, n10_bit_register_file_1_readacc, n10_bit_register_file_1_readdata_1,
       n10_bit_register_file_1_readdata_2, PC_q, ram_1_data, rom_1_data, shifter_1_out;

  Register #(.width(10)) PC (.D(multiplexer_1_out), .Q(PC_q), .clk(clock_1_out), .clr(in_1));  // open: en
  Clock clock_1 (.out(clock_1_out));
  Multiplexer #(.width(10), .enable("false")) multiplexer_1 (
    .in0(multiplexer_5_out), .in1(shifter_1_out), .out(multiplexer_1_out), .sel(control_unit_1_unconditional));
  Adder #(.width(10)) adder_1 (.a(10'h4), .b(PC_q), .out(adder_1_out));  // open: cin, cout
  ROM #(.addrWidth(10), .dataWidth(10)) rom_1 (.addr(PC_q), .data(rom_1_data));  // open: sel
  Shifter #(.width(10)) shifter_1 (.in(multiplexer_2_out), .\dist (4'b0010), .out(shifter_1_out));
  Multiplexer #(.width(10), .enable("false")) multiplexer_2 (
    .in0(bit_extender_1_out), .in1(bit_extender_2_out), .out(multiplexer_2_out),
    .sel(control_unit_1_unconditional));
  _10_bit_Register_File u_10_bit_register_file_1 (
    .writeData(multiplexer_3_out), .clk(clock_1_out), .regWrite(control_unit_1_move),
    .readRegister_1(rom_1_data[5:3]), .readRegister_2(rom_1_data[2:0]),
    .readData_1(n10_bit_register_file_1_readdata_1), .readData_2(n10_bit_register_file_1_readdata_2),
    .moveTo(rom_1_data[5:3]), .\output (Output), .WriteAcc(multiplexer_8_out),
    .accWrite(control_unit_1_writeacc), .readAcc(n10_bit_register_file_1_readacc));
  assign bit_extender_1_out = {{7{1'b0}}, rom_1_data[2:0]};  // Bit_Extender bit_extender_1
  assign bit_extender_2_out = {{4{1'b0}}, rom_1_data[5:0]};  // Bit_Extender bit_extender_2
  Control_Unit control_unit_1 (
    .Opcode(rom_1_data[9:6]), .AluOp(control_unit_1_aluop), .Bin(control_unit_1_bin),
    .Ain(control_unit_1_ain), .Immidiate(control_unit_1_immidiate),
    .Unconditional(control_unit_1_unconditional), .Branch(control_unit_1_branch), .load(control_unit_1_load),
    .readMemory(control_unit_1_readmemory), .move(control_unit_1_move), .writeAcc(control_unit_1_writeacc),
    .notEqual(control_unit_1_notequal));
  Adder #(.width(10)) adder_2 (.a(adder_1_out), .b(shifter_1_out), .out(adder_2_out));  // open: cin, cout
  Multiplexer #(.width(10), .enable("false")) multiplexer_3 (
    .in0(n10_bit_register_file_1_readdata_2), .in1(bit_extender_1_out), .out(multiplexer_3_out),
    .sel(control_unit_1_immidiate));
  and and_1 (and_1_out, control_unit_1_branch, multiplexer_6_out);
  Multiplexer #(.width(10), .enable("false")) multiplexer_4 (
    .in0(multiplexer_3_out), .in1(n10_bit_register_file_1_readacc), .out(multiplexer_4_out),
    .sel(control_unit_1_branch));
  Multiplexer #(.width(10), .enable("false")) multiplexer_5 (
    .in0(adder_1_out), .in1(adder_2_out), .out(multiplexer_5_out), .sel(and_1_out));
  Multiplexer #(.enable("false")) multiplexer_6 (
    .in0(multiplexer_7_out), .in1(control_unit_1_notequal), .out(multiplexer_6_out),
    .sel(control_unit_1_notequal));
  Multiplexer #(.select(2), .enable("false")) multiplexer_7 (
    .in0(1'b0), .in1(1'b0), .in2(n10_bit_alu_1_zero), .in3(n10_bit_alu_1_less), .out(multiplexer_7_out),
    .sel(control_unit_1_aluop));
  _10_bit_ALU u_10_bit_alu_1 (
    .Ainvert(control_unit_1_ain), .Binvert(control_unit_1_bin), .OpA(n10_bit_register_file_1_readdata_1),
    .OpB(multiplexer_4_out), .Zero(n10_bit_alu_1_zero), .Result(n10_bit_alu_1_result),
    .OpSelect(control_unit_1_aluop), .Less(n10_bit_alu_1_less));  // open: Cout, Overflow
  Multiplexer #(.width(10), .enable("false")) multiplexer_8 (
    .in0(n10_bit_alu_1_result), .in1(ram_1_data), .out(multiplexer_8_out), .sel(control_unit_1_readmemory));
  RAM #(.addrWidth(10), .dataWidth(10)) ram_1 (
    .addr(n10_bit_alu_1_result), .data(ram_1_data), .clk(clock_1_out), .ld(control_unit_1_load));  // open: sel, clr
  assign ram_1_data = not_1_out ? n10_bit_register_file_1_readacc : 10'bz;  // Controlled_Buffer controlled_buffer_1
  not not_1 (not_1_out, control_unit_1_load);

  // Notes on the sheet:
  //   contents of rom_1 (hex, n*v repeats v):
  //   20a 0 0 0 d7 0 0 0 97 0 0 0 1ba 0 0 0 2e5 0 0 0 263 0 0 0 2a8 0 0 0 2c9 0 0 0 8 0 0 0 48 0 0 0 108 0
  //   0 0 1f6 0 0 0 2a3 0 0 0 312 11*0 2a3 0 0 0 2ff 0 0 0 3a5 0 0 0 374 19*0 2e3 0 0 0 3c6 27*0 2e3
endmodule

module Control_Unit (
  input  [3:0] Opcode,
  output [1:0] AluOp,
  output Bin,
  output Branch,
  output Immidiate,
  output Unconditional,
  output load,
  output readMemory,
  output move,
  output notEqual,
  output writeAcc,
  output Ain
);

  wire and_6_out, and_7_out, not_1_out, not_2_out, not_3_out, not_4_out, not_5_out, not_6_out, not_7_out;
  wire [1:0] multiplexer_1_out;

  not not_1 (not_1_out, Opcode[3]);
  not not_2 (not_2_out, Opcode[1]);
  not not_3 (not_3_out, Opcode[0]);
  and and_1 (Ain, not_1_out, Opcode[2], not_2_out, not_3_out);
  Multiplexer #(.select(2), .width(2), .enable("false")) multiplexer_1 (
    .in0(2'b10), .in1(2'b10), .in2(2'b10), .in3(2'b11), .out(multiplexer_1_out), .sel(Opcode[2:1]));
  not not_4 (not_4_out, Opcode[2]);
  not not_5 (not_5_out, Opcode[1]);
  not not_6 (not_6_out, Opcode[0]);
  and and_2 (Unconditional, Opcode[0], Opcode[1], Opcode[2], Opcode[3]);
  nand nand_1 (load, Opcode[3], not_4_out, not_5_out, Opcode[0]);
  and and_3 (readMemory, Opcode[3], not_4_out, Opcode[1], not_6_out);
  and and_4 (move, not_4_out, Opcode[1], Opcode[0]);
  and and_5 (notEqual, Opcode[3], Opcode[2], not_5_out, Opcode[0]);
  not not_7 (not_7_out, load);
  and and_6 (and_6_out, Opcode[0], Opcode[2]);
  and and_7 (and_7_out, Opcode[3], Opcode[2]);
  Multiplexer #(.width(2), .enable("false")) multiplexer_2 (
    .in0(Opcode[1:0]), .in1(multiplexer_1_out), .out(AluOp), .sel(Opcode[3]));
  nor nor_1 (writeAcc, move, not_7_out, and_6_out, and_7_out);
  and and_8 (Branch, Opcode[2], Opcode[3]);

  assign Bin = Opcode[2];
  assign Immidiate = Opcode[3];
endmodule
