// Logisim project 10-bitRegisterFile.circ as structural Verilog
module _10_bit_Register_File (
  input  [9:0] writeData,
  input  [2:0] moveTo,
  input  [9:0] WriteAcc,
  input  clk,
  input  accWrite,
  input  regWrite,
  input  [2:0] readRegister_1,
  input  [2:0] readRegister_2,
  output [9:0] readData_1,
  output [9:0] readData_2,
  output [9:0] \output ,
  output [9:0] readAcc
);

  wire and_1_out, and_2_out, and_3_out, and_4_out, and_5_out, and_6_out, and_7_out, and_8_out,
       decoder_1_out0, decoder_1_out1, decoder_1_out2, decoder_1_out3, decoder_1_out4, decoder_1_out5,
       decoder_1_out6, decoder_1_out7, or_1_out;
  wire [9:0] multiplexer_1_out, s0_q, s1_q, s2_q, t0_q, t1_q, zero_q;

  Decoder #(.select(3), .enable("false")) decoder_1 (
    .out0(decoder_1_out0), .out1(decoder_1_out1), .out2(decoder_1_out2), .out3(decoder_1_out3),
    .out4(decoder_1_out4), .out5(decoder_1_out5), .out6(decoder_1_out6), .out7(decoder_1_out7), .sel(moveTo));
  and and_1 (and_1_out, decoder_1_out0, regWrite);
  and and_2 (and_2_out, decoder_1_out1, regWrite);
  and and_3 (and_3_out, decoder_1_out2, regWrite);
  and and_4 (and_4_out, decoder_1_out3, regWrite);
  and and_5 (and_5_out, decoder_1_out4, regWrite);
  and and_6 (and_6_out, decoder_1_out5, regWrite);
  and and_7 (and_7_out, decoder_1_out6, regWrite);
  and and_8 (and_8_out, decoder_1_out7, regWrite);
  Register #(.width(10)) zero (.D(writeData), .en(and_1_out), .Q(zero_q), .clk(clk));  // open: clr
  Register #(.width(10)) s0 (.D(writeData), .en(and_2_out), .Q(s0_q), .clk(clk));  // open: clr
  Register #(.width(10)) s1 (.D(writeData), .en(and_3_out), .Q(s1_q), .clk(clk));  // open: clr
  Register #(.width(10)) s2 (.D(writeData), .en(and_4_out), .Q(s2_q), .clk(clk));  // open: clr
  Register #(.width(10)) t0 (.D(writeData), .en(and_5_out), .Q(t0_q), .clk(clk));  // open: clr
  Register #(.width(10)) t1 (.D(writeData), .en(and_6_out), .Q(t1_q), .clk(clk));  // open: clr
  Register #(.width(10)) io (.D(writeData), .en(and_7_out), .Q(\output ), .clk(clk));  // open: clr
  Multiplexer #(.width(10), .enable("false")) multiplexer_1 (
    .in0(writeData), .in1(WriteAcc), .out(multiplexer_1_out), .sel(accWrite));
  or or_1 (or_1_out, and_8_out, accWrite);
  Register #(.width(10)) acc (.D(multiplexer_1_out), .en(or_1_out), .Q(readAcc), .clk(clk));  // open: clr
  Multiplexer #(.select(3), .width(10), .enable("false")) multiplexer_2 (
    .in0(zero_q), .in1(s0_q), .in2(s1_q), .in3(s2_q), .in4(t0_q), .in5(t1_q), .in6(\output ), .in7(readAcc),
    .out(readData_1), .sel(readRegister_1));
  Multiplexer #(.select(3), .width(10), .enable("false")) multiplexer_3 (
    .in0(zero_q), .in1(s0_q), .in2(s1_q), .in3(s2_q), .in4(t0_q), .in5(t1_q), .in6(\output ), .in7(readAcc),
    .out(readData_2), .sel(readRegister_2));
endmodule
