// Logisim project 10bitALU.circ as structural Verilog
module _1_bit_ALU (
  input  Less,
  input  Ainvert,
  input  Binvert,
  input  Cin,
  input  [1:0] OpSelect,
  input  opB,
  input  opA,
  output res,
  output Set,
  output Cout
);

  wire and_1_out, multiplexer_1_out, multiplexer_2_out, not_1_out, not_2_out, or_1_out;

  not not_1 (not_1_out, opB);
  Multiplexer #(.enable("false")) multiplexer_1 (.in0(opB), .in1(not_1_out), .out(multiplexer_1_out), .sel(Binvert));
  not not_2 (not_2_out, opA);
  Multiplexer #(.enable("false")) multiplexer_2 (.in0(opA), .in1(not_2_out), .out(multiplexer_2_out), .sel(Ainvert));
  and and_1 (and_1_out, multiplexer_2_out, multiplexer_1_out);
  or or_1 (or_1_out, multiplexer_2_out, multiplexer_1_out);
  Adder #(.width(1)) adder_1 (.a(multiplexer_2_out), .b(multiplexer_1_out), .out(Set), .cin(Cin), .cout(Cout));
  Multiplexer #(.select(2), .enable("false")) multiplexer_3 (
    .in0(and_1_out), .in1(or_1_out), .in2(Set), .in3(Less), .out(res), .sel(OpSelect));
endmodule

module _10_bit_ALU (
  input  Ainvert,
  input  [1:0] OpSelect,
  input  Binvert,
  input  [9:0] OpA,
  input  [9:0] OpB,
  output Less,
  output Zero,
  output [9:0] Result,
  output Cout,
  output Overflow
);

  wire n1_bit_alu_1_cout, n1_bit_alu_2_cout, n1_bit_alu_3_cout, n1_bit_alu_4_cout, n1_bit_alu_5_cout,
       n1_bit_alu_6_cout, n1_bit_alu_7_cout, n1_bit_alu_8_cout, n1_bit_alu_9_cout, n1_bit_alu_10_set;

  _1_bit_ALU u_1_bit_alu_1 (
    .res(Less), .Cout(n1_bit_alu_1_cout), .Ainvert(Ainvert), .Binvert(Binvert), .Cin(Binvert),
    .OpSelect(OpSelect), .opB(OpB[0]), .opA(OpA[0]), .Less(n1_bit_alu_10_set));  // open: Set
  _1_bit_ALU u_1_bit_alu_2 (
    .res(Result[1]), .Cout(n1_bit_alu_2_cout), .Ainvert(Ainvert), .Binvert(Binvert), .Cin(n1_bit_alu_1_cout),
    .OpSelect(OpSelect), .opB(OpB[1]), .opA(OpA[1]), .Less(1'b0));  // open: Set
  _1_bit_ALU u_1_bit_alu_3 (
    .res(Result[2]), .Cout(n1_bit_alu_3_cout), .Ainvert(Ainvert), .Binvert(Binvert), .Cin(n1_bit_alu_2_cout),
    .OpSelect(OpSelect), .opB(OpB[2]), .opA(OpA[2]), .Less(1'b0));  // open: Set
  _1_bit_ALU u_1_bit_alu_4 (
    .res(Result[3]), .Cout(n1_bit_alu_4_cout), .Ainvert(Ainvert), .Binvert(Binvert), .Cin(n1_bit_alu_3_cout),
    .OpSelect(OpSelect), .opB(OpB[3]), .opA(OpA[3]), .Less(1'b0));  // open: Set
  _1_bit_ALU u_1_bit_alu_5 (
    .res(Result[4]), .Cout(n1_bit_alu_5_cout), .Ainvert(Ainvert), .Binvert(Binvert), .Cin(n1_bit_alu_4_cout),
    .OpSelect(OpSelect), .opB(OpB[4]), .opA(OpA[4]), .Less(1'b0));  // open: Set
  _1_bit_ALU u_1_bit_alu_6 (
    .res(Result[5]), .Cout(n1_bit_alu_6_cout), .Ainvert(Ainvert), .Binvert(Binvert), .Cin(n1_bit_alu_5_cout),
    .OpSelect(OpSelect), .opB(OpB[5]), .opA(OpA[5]), .Less(1'b0));  // open: Set
  _1_bit_ALU u_1_bit_alu_7 (
    .res(Result[6]), .Cout(n1_bit_alu_7_cout), .Ainvert(Ainvert), .Binvert(Binvert), .Cin(n1_bit_alu_6_cout),
    .OpSelect(OpSelect), .opB(OpB[6]), .opA(OpA[6]), .Less(1'b0));  // open: Set
  _1_bit_ALU u_1_bit_alu_8 (
    .res(Result[7]), .Cout(n1_bit_alu_8_cout), .Ainvert(Ainvert), .Binvert(Binvert), .Cin(n1_bit_alu_7_cout),
    .OpSelect(OpSelect), .opB(OpB[7]), .opA(OpA[7]), .Less(1'b0));  // open: Set
  _1_bit_ALU u_1_bit_alu_9 (
    .res(Result[8]), .Cout(n1_bit_alu_9_cout), .Ainvert(Ainvert), .Binvert(Binvert), .Cin(n1_bit_alu_8_cout),
    .OpSelect(OpSelect), .opB(OpB[8]), .opA(OpA[8]), .Less(1'b0));  // open: Set
  _1_bit_ALU u_1_bit_alu_10 (
    .res(Result[9]), .Cout(Cout), .Ainvert(Ainvert), .Binvert(Binvert), .Cin(n1_bit_alu_9_cout),
    .OpSelect(OpSelect), .opB(OpB[9]), .opA(OpA[9]), .Less(1'b0), .Set(n1_bit_alu_10_set));
  nor nor_1 (Zero, Less, Result[1], Result[2], Result[3], Result[4], Result[5], Result[6], Result[7], Result[8], Result[9]);
  xor xor_1 (Overflow, Cout, n1_bit_alu_9_cout);

  assign Result[0] = Less;
endmodule
